// Digital circuit ALU.dig as structural Verilog
module ALU (
  input  [7:0] inbus,
  input  [1:0] op,
  input  CLk,
  input  Begin,
  input  RST,
  input  c_in,
  output [7:0] outbus
);

  wire c0, c2, c3, c4, c7, c8, or_2_out, undriven;
  wire [0:0] or_1_out;
  wire [7:0] driver_1_out, driver_2_out, M_q, multiplexer_1_out, Parallel_Adder_z, Q_q, xor_1_out;

  or or_1 (or_1_out[0], c0, c3);
  or or_2 (or_2_out, c0, c3, c3);
  Multiplexer #(.Selector_Bits(2)) multiplexer_1 (
    .sel({c3, or_1_out[0]}), .in_0(1'b0), .in_1(inbus[0]), .in_2(Parallel_Adder_z[0]),
    .out(multiplexer_1_out[0]));  // open: in_3
  Register #(.Bits(8)) A (.D(multiplexer_1_out), .en(or_2_out));  // open: C, Q
  // Probe on driver_1_out
  assign driver_1_out = c3 ? inbus : 8'bz;  // Driver driver_1
  Register #(.Bits(8)) Q (.D(driver_1_out), .C(~CLk), .en(c3), .Q(Q_q));
  ALU_CU alu_cu_1 (
    .BGN(Begin), .RST(RST), .CLK(CLk), .CNT7(1'b0), .Q0(1'b0), .Q_1(1'b0), .A7(1'b0), .OP(op), .c0(c0),
    .c0_2(c3), .c1(c3), .c2(c2), .c3(c3), .c4(c4), .c7(c7), .c8(c8));  // open: cR, cL, c5, c6, c7_5
  // Probe on Q_q
  Register Q__1 (.D(undriven), .C(~CLk));  // open: en, Q
  assign driver_2_out = c2 ? inbus : 8'bz;  // Driver driver_2
  // Probe on driver_2_out
  Register #(.Bits(8)) M (.D(driver_2_out), .C(~CLk), .en(c2), .Q(M_q));
  assign xor_1_out = {8{c4}} ^ M_q;  // XOr xor_1, 8 bits wide
  // Probe on M_q
  RCA8 Parallel_Adder (.c_in(c_in), .Y(xor_1_out), .X(Q_q), .Z(Parallel_Adder_z));  // open: c_out
  assign outbus = c3 ? Parallel_Adder_z : 8'bz;  // Driver driver_3
  // Pins of 1 and 8 bits meet at inbus
  // Pins of 1 and 8 bits meet at Parallel_Adder_z
  // Pins of 1 and 8 bits meet at multiplexer_1_out
  // Pins of 1 and 8 bits meet at {8{1'b0}}
endmodule
